# Fritzing sketch MultipleToggleSwtiches (saved by Fritzing 0.9.2b)
breadboards: 1

parts:
  Part1 = Arduino Uno (Rev3)
  S1 = Toggle Switch [package=THT]
  R3 = Resistor [tolerance=±20% resistance=10k package=THT]
  S2 = Toggle Switch [package=THT]
  R4 = Resistor [tolerance=±20% resistance=10k package=THT]
  S3 = Toggle Switch [package=THT]
  R5 = Resistor [tolerance=±20% resistance=10k package=THT]
  LED1 = LED - 5mm [color="Red (633nm)" package="5 mm [THT]"]
  LED2 = LED - 5mm [color="Red (633nm)" package="5 mm [THT]"]
  LED3 = LED - 5mm [color="Red (633nm)" package="5 mm [THT]"]
  R6 = Resistor [tolerance=±10% resistance=330 package=THT]
  R7 = Resistor [tolerance=±10% resistance=330 package=THT]
  R8 = Resistor [tolerance=±10% resistance=330 package=THT]

nets:
  N1: Part1.D2, S1.COM
  N2: Part1.D3_PWM, S2.COM
  N3: Part1.D4, S3.COM
  N4: Part1.D5_PWM, LED1.anode
  N5: Part1.D6_PWM, LED2.anode
  N6: Part1.D7, LED3.anode
  N7: Part1.5V, S1.L2, S2.L2, S3.L2
  N8: Part1.GND, R3.Pin_0, R4.Pin_0, R5.Pin_0, R6.Pin_1, R7.Pin_1, R8.Pin_1
  N9: S1.L1, R3.Pin_1
  N10: S2.L1, R4.Pin_1
  N11: S3.L1, R5.Pin_1
  N12: LED1.cathode, R6.Pin_0
  N13: LED2.cathode, R7.Pin_0
  N14: LED3.cathode, R8.Pin_0
